// Digital circuit ALU.dig as structural Verilog
module ALU (
  input  [15:0] Reg_in,
  input  [8:0] immediate,
  input  ADD_ALU,
  input  SUB_ALU,
  input  MUL_ALU,
  input  DIV_ALU,
  input  LSR_ALU,
  input  LSL_ALU,
  input  RSR_ALU,
  input  RSL_ALU,
  input  MOV_ALU,
  input  MOD_ALU,
  input  AND_ALU,
  input  OR_ALU,
  input  XOR_ALU,
  input  NOT_ALU,
  input  CMP_ALU,
  input  TST_ALU,
  input  [15:0] MOV_TBD,
  output [15:0] ALU_ACC,
  output [15:0] ALU_logical,
  output [15:0] ALU
);

  wire nor_1_out;
  wire [0:0] TBD_eq;
  wire [1:0] conv_oh_to_num_1_out1, conv_oh_to_num_1_out3;
  wire [2:0] Logical;
  wire [15:0] adder_16b_s, and_1_out, div_1_q, div_1_r, LSL_out, LSR_out, mul_1_mul, not_1_out, or_1_out,
       RSL_out, RSR_out, sub_1_s, xor_1_out;
  wire [31:16] mul_1_mul_2;

  Add #(.Bits(16)) adder_16b (.a(Reg_in), .b({{7{1'b0}}, immediate}), .c_i(1'b0), .s(adder_16b_s));  // open: c_o
  Sub #(.Bits(16)) sub_1 (.a(Reg_in), .b({{7{1'b0}}, immediate}), .c_i(1'b0), .s(sub_1_s));  // open: c_o
  Mul #(.Bits(16), .Signed("true")) mul_1 (.a(Reg_in), .b({{7{1'b0}}, immediate}), .mul({mul_1_mul_2, mul_1_mul}));
  Div #(.Bits(16), .Signed("true")) div_1 (.a(Reg_in), .b({{7{1'b0}}, immediate}), .q(div_1_q), .r(div_1_r));
  Comparator #(.Bits(16), .Signed("true")) TBD (
    .a({{7{1'b0}}, immediate}), .b(Reg_in), .eq(TBD_eq[0]));  // open: gt, lt
  assign and_1_out = Reg_in & {{7{1'b0}}, immediate};  // And and_1, 16 bits wide
  assign or_1_out = {{7{1'b0}}, immediate} | Reg_in;  // Or or_1, 16 bits wide
  assign xor_1_out = Reg_in ^ {{7{1'b0}}, immediate};  // XOr xor_1, 16 bits wide
  assign not_1_out = ~Reg_in;  // Not not_1, 16 bits wide
  BarrelShifter #(.Bits(16), .barrelSigned("true"), .direction("right")) LSR (
    .in(Reg_in), .shift(immediate[5:0]), .out(LSR_out));
  BarrelShifter #(.Bits(16), .barrelSigned("true")) LSL (.in(Reg_in), .shift(immediate[5:0]), .out(LSL_out));
  BarrelShifter #(.Bits(16), .barrelShifterMode("rotate"), .barrelSigned("true"), .direction("right")) RSR (
    .in(Reg_in), .shift(immediate[5:0]), .out(RSR_out));
  BarrelShifter #(.Bits(16), .barrelShifterMode("rotate"), .barrelSigned("true")) RSL (
    .in(Reg_in), .shift(immediate[5:0]), .out(RSL_out));
  Multiplexer #(.Bits(16), .Selector_Bits(3)) multiplexer_1 (
    .sel(Logical), .in_0(16'hfefe), .in_1(and_1_out), .in_2(or_1_out), .in_3(xor_1_out), .in_4(not_1_out),
    .in_5(16'hfefe), .in_6(16'hfefe), .in_7(16'hfefe), .out(ALU_logical));
  conv_OH_to_Num_LogicalOPs conv_oh_to_num_logicalops_1 (
    .AND(AND_ALU), .OR(OR_ALU), .XOR(XOR_ALU), .NOT(NOT_ALU), .out1(Logical[2]), .out2(Logical[1]),
    .out3(Logical[0]));
  conv_OH_to_Num conv_oh_to_num_1 (
    .ADD(ADD_ALU), .SUB(SUB_ALU), .MUL(MUL_ALU), .DIV(DIV_ALU), .LSR(LSR_ALU), .LSL(LSL_ALU), .RSR(RSR_ALU),
    .RSL(RSL_ALU), .MOV(MOV_ALU), .MOD(MOD_ALU), .CMP(CMP_ALU), .TST(TST_ALU),
    .out1(conv_oh_to_num_1_out1[1]), .out2(conv_oh_to_num_1_out1[0]), .out3(conv_oh_to_num_1_out3[1]),
    .out4(conv_oh_to_num_1_out3[0]));
  nor nor_1 (nor_1_out, AND_ALU, OR_ALU, XOR_ALU, NOT_ALU);
  Multiplexer #(.Bits(16), .Selector_Bits(4)) multiplexer_2 (
    .sel({conv_oh_to_num_1_out1, conv_oh_to_num_1_out3}), .in_0(16'hfefe), .in_1(adder_16b_s),
    .in_2(sub_1_s), .in_3(mul_1_mul), .in_4(div_1_q), .in_5(LSR_out), .in_6(LSL_out), .in_7(RSR_out),
    .in_8(RSL_out), .in_9(MOV_TBD), .in_10(div_1_r), .in_11({{15{1'b0}}, TBD_eq[0]}), .in_12(16'ha0a0),
    .in_13({16{1'b1}}), .in_14({16{1'b1}}), .in_15({16{1'b1}}), .out(ALU_ACC));
  Multiplexer #(.Bits(16)) multiplexer_3 (.sel(nor_1_out), .in_0(ALU_logical), .in_1(ALU_ACC), .out(ALU));

  // Notes on the sheet:
  //   Convert 9 bits to 16 bits
endmodule
