// Digital circuit Control_Unit_Impl.dig as structural Verilog
module Control_Unit_Impl (
  input  [5:0] opcode,
  output typeOfOperand,
  output en_IR,
  output en_PC,
  output ADD_ALU,
  output SUB_ALU,
  output MUL_ALU,
  output DIV_ALU,
  output Load,
  output Store,
  output LSR_ALU,
  output LSL_ALU,
  output RSR_ALU,
  output RSL_ALU,
  output MOV_ALU,
  output MOD_ALU,
  output AND_ALU,
  output OR_ALU,
  output XOR_ALU,
  output NOT_ALU,
  output CMP_ALU,
  output TST_ALU,
  output INC_ALU,
  output DEC_ALU,
  output POP,
  output PUSH,
  output HLT
);

  wire not_1_out, not_2_out, not_3_out, not_4_out, not_5_out, not_6_out, not_7_out, not_8_out, not_9_out,
       not_10_out, not_11_out, not_12_out, not_13_out, not_14_out, not_15_out, not_16_out, not_17_out,
       not_18_out, not_19_out, not_20_out, not_21_out, not_22_out, not_23_out, not_24_out, not_25_out,
       not_26_out, not_27_out, not_28_out, not_29_out, not_30_out, not_31_out, not_32_out, not_33_out,
       not_34_out, not_35_out, not_36_out, not_37_out, not_38_out, not_39_out, not_40_out, not_41_out,
       not_42_out, not_43_out, not_44_out, not_45_out, not_46_out, not_47_out, not_48_out, not_49_out,
       not_50_out, not_51_out, not_52_out, not_53_out, not_54_out, not_55_out, not_56_out, not_57_out,
       not_58_out, not_59_out, not_60_out, not_61_out;

  not not_1 (not_1_out, opcode[4]);
  not not_2 (not_2_out, opcode[2]);
  not not_3 (not_3_out, opcode[1]);
  not not_4 (not_4_out, opcode[4]);
  not not_5 (not_5_out, opcode[2]);
  not not_6 (not_6_out, opcode[0]);
  not not_7 (not_7_out, opcode[3]);
  not not_8 (not_8_out, opcode[2]);
  not not_9 (not_9_out, opcode[1]);
  not not_10 (not_10_out, opcode[0]);
  not not_11 (not_11_out, opcode[3]);
  not not_12 (not_12_out, opcode[2]);
  not not_13 (not_13_out, opcode[1]);
  not not_14 (not_14_out, opcode[5]);
  not not_15 (not_15_out, opcode[4]);
  not not_16 (not_16_out, opcode[5]);
  not not_17 (not_17_out, opcode[4]);
  not not_18 (not_18_out, opcode[3]);
  not not_19 (not_19_out, opcode[2]);
  not not_20 (not_20_out, opcode[1]);
  not not_21 (not_21_out, opcode[4]);
  not not_22 (not_22_out, opcode[2]);
  not not_23 (not_23_out, opcode[0]);
  not not_24 (not_24_out, opcode[4]);
  not not_25 (not_25_out, opcode[1]);
  not not_26 (not_26_out, opcode[0]);
  not not_27 (not_27_out, opcode[4]);
  not not_28 (not_28_out, opcode[1]);
  not not_29 (not_29_out, opcode[4]);
  not not_30 (not_30_out, opcode[0]);
  not not_31 (not_31_out, opcode[4]);
  not not_32 (not_32_out, opcode[3]);
  not not_33 (not_33_out, opcode[2]);
  not not_34 (not_34_out, opcode[0]);
  not not_35 (not_35_out, opcode[3]);
  not not_36 (not_36_out, opcode[2]);
  not not_37 (not_37_out, opcode[3]);
  not not_38 (not_38_out, opcode[1]);
  // Not not_39 has open pins: in=open, out=not_39_out
  not not_40 (not_40_out, opcode[3]);
  not not_41 (not_41_out, opcode[1]);
  not not_42 (not_42_out, opcode[3]);
  not not_43 (not_43_out, opcode[2]);
  not not_44 (not_44_out, opcode[1]);
  not not_45 (not_45_out, opcode[0]);
  not not_46 (not_46_out, opcode[2]);
  not not_47 (not_47_out, opcode[1]);
  not not_48 (not_48_out, opcode[2]);
  not not_49 (not_49_out, opcode[0]);
  not not_50 (not_50_out, opcode[2]);
  not not_51 (not_51_out, opcode[5]);
  not not_52 (not_52_out, opcode[1]);
  not not_53 (not_53_out, opcode[0]);
  not not_54 (not_54_out, opcode[5]);
  not not_55 (not_55_out, opcode[1]);
  not not_56 (not_56_out, opcode[5]);
  not not_57 (not_57_out, opcode[4]);
  not not_58 (not_58_out, opcode[3]);
  not not_59 (not_59_out, opcode[2]);
  not not_60 (not_60_out, opcode[1]);
  not not_61 (not_61_out, opcode[0]);
  and and_1 (ADD_ALU, opcode[5], not_1_out, opcode[3], not_2_out, opcode[0], not_3_out);
  and and_2 (SUB_ALU, opcode[5], not_4_out, opcode[3], not_5_out, opcode[1], not_6_out);
  and and_3 (MUL_ALU, opcode[5], opcode[4], not_7_out, not_8_out, not_9_out, not_10_out);
  and and_4 (DIV_ALU, opcode[5], opcode[4], not_11_out, not_12_out, not_13_out, opcode[0]);
  and and_5 (Load, not_14_out, not_15_out, opcode[3], opcode[2], opcode[1], opcode[0]);
  and and_6 (Store, not_16_out, not_17_out, not_18_out, not_19_out, not_20_out, opcode[0]);
  and and_7 (LSR_ALU, opcode[5], not_21_out, opcode[3], not_22_out, opcode[1], not_23_out);
  and and_8 (LSL_ALU, opcode[5], not_24_out, opcode[3], opcode[2], not_25_out, not_26_out);
  and and_9 (RSR_ALU, opcode[5], not_27_out, opcode[3], opcode[2], not_28_out, opcode[0]);
  and and_10 (RSL_ALU, opcode[5], not_29_out, opcode[3], opcode[2], opcode[1], not_30_out);
  and and_11 (MOV_ALU, opcode[5], not_31_out, opcode[3], opcode[2], opcode[1], opcode[0]);
  and and_12 (MOD_ALU, opcode[5], opcode[4], not_32_out, not_33_out, opcode[1], not_34_out);
  and and_13 (AND_ALU, opcode[5], opcode[4], not_35_out, not_36_out, opcode[1], opcode[0]);
  and and_14 (OR_ALU, opcode[5], opcode[4], not_37_out, opcode[2], not_38_out, not_39_out);
  and and_15 (XOR_ALU, opcode[5], opcode[4], not_40_out, opcode[2], not_41_out, opcode[1]);
  and and_16 (NOT_ALU, opcode[5], opcode[4], not_42_out, opcode[2], opcode[1], opcode[0]);
  and and_17 (CMP_ALU, opcode[5], opcode[4], opcode[3], not_43_out, not_44_out, not_45_out);
  and and_18 (TST_ALU, opcode[5], opcode[4], opcode[3], not_46_out, not_47_out, opcode[0]);
  and and_19 (INC_ALU, opcode[5], opcode[4], opcode[3], not_48_out, opcode[1], not_49_out);
  and and_20 (DEC_ALU, opcode[5], opcode[4], opcode[3], not_50_out, opcode[1], opcode[0]);
  and and_21 (POP, not_51_out, opcode[4], opcode[3], opcode[2], not_52_out, not_53_out);
  and and_22 (PUSH, not_54_out, opcode[4], opcode[3], opcode[2], not_55_out, opcode[0]);
  and and_23 (HLT, not_56_out, not_57_out, not_58_out, not_59_out, not_60_out, not_61_out);
  opcode_is_branch opcode_is_branch_1 (
    .A(opcode[5]), .B(opcode[4]), .C(opcode[3]), .D(opcode[2]), .E(opcode[1]), .F(opcode[0]),
    .Y(typeOfOperand));

  assign en_IR = 1'b1;
  assign en_PC = 1'b1;
endmodule
