// Digital circuit FLAG_Register.dig as structural Verilog
module FLAG_Register (
  input  Clk,
  input  N_in,
  input  Z_in,
  input  C_in,
  input  V_in,
  output N_out,
  output Z_out,
  output C_out,
  output V_out
);

  D_FF d_ff_1 (.D(N_in), .C(Clk), .Q(N_out));  // open: nQ
  D_FF d_ff_2 (.D(Z_in), .C(Clk), .Q(Z_out));  // open: nQ
  D_FF d_ff_3 (.D(C_in), .C(Clk), .Q(C_out));  // open: nQ
  D_FF d_ff_4 (.D(V_in), .C(Clk), .Q(V_out));  // open: nQ

  // Notes on the sheet:
  //   Clk: pin 1
endmodule
