// Digital circuit InstructionRegister.dig as structural Verilog
module InstructionRegister (
  input  [9:0] D_in,
  input  clk,
  input  enable,
  input  typeOfOperand,
  output reg_no,
  output [8:0] immediate,
  output [9:0] adress
);

  wire not_1_out, not_2_out;
  wire [9:0] instructionRegister_q;

  Register #(.Bits(10)) instructionRegister (.D(D_in), .C(clk), .en(enable), .Q(instructionRegister_q));
  assign reg_no = not_1_out ? instructionRegister_q[9] : 1'bz;  // Driver driver_1
  not not_1 (not_1_out, typeOfOperand);
  assign immediate = not_2_out ? instructionRegister_q[8:0] : 9'bz;  // Driver driver_2
  not not_2 (not_2_out, typeOfOperand);
  assign adress = typeOfOperand ? instructionRegister_q : 10'bz;  // Driver driver_3

  // Notes on the sheet:
  //   D_in: It takes 1 word = 16 bits from Main Memory
  //   clk: Hz: 10
  //   typeOfOperand: Check which of 2 possible configurations it is found
  //   0= register addr + immediate
  //   1= adress (10 bits)
  //   Comes from Control Unit
endmodule
