// Digital circuit Program Counter.dig as structural Verilog
module Program_Counter (
  input  [9:0] ADR_in,
  input  en,
  input  clk,
  input  jmp_sel,
  output [9:0] out,
  output ovf
);

  wire [9:0] Adder_10b_s, multiplexer_1_out;

  Multiplexer #(.Bits(10)) multiplexer_1 (.sel(jmp_sel), .in_0(out), .in_1(ADR_in), .out(multiplexer_1_out));
  Add #(.Bits(10)) Adder_10b (.a(multiplexer_1_out), .b(10'h1), .c_i(1'b0), .s(Adder_10b_s), .c_o(ovf));
  Register #(.Bits(10)) CNT (.D(Adder_10b_s), .C(clk), .en(en), .Q(out));
endmodule
