// Digital circuit Registers.dig as structural Verilog
module Registers (
  input  clk,
  input  sel_reg,
  input  read_adr,
  input  [15:0] D_in,
  input  W_en,
  output [15:0] REG_out
);

  wire and_1_out, and_2_out, decoder_1_out_0, decoder_1_out_1;
  wire [15:0] X_q, Y_q;

  Decoder decoder_1 (.sel(sel_reg), .out_0(decoder_1_out_0), .out_1(decoder_1_out_1));
  and and_1 (and_1_out, decoder_1_out_0, W_en);
  and and_2 (and_2_out, decoder_1_out_1, W_en);
  Register #(.Bits(16)) X (.D(D_in), .C(clk), .en(and_1_out), .Q(X_q));
  Register #(.Bits(16)) Y (.D(D_in), .C(clk), .en(and_2_out), .Q(Y_q));
  Multiplexer #(.Bits(16)) multiplexer_1 (.sel(read_adr), .in_0(X_q), .in_1(Y_q), .out(REG_out));

  // Notes on the sheet:
  //   clk: Hz: 5
endmodule
