// Digital circuit conv_OH_to_Num.dig as structural Verilog
module conv_OH_to_Num (
  input  ADD,
  input  SUB,
  input  MUL,
  input  DIV,
  input  LSR,
  input  LSL,
  input  RSR,
  input  RSL,
  input  MOV,
  input  MOD,
  input  CMP,
  input  TST,
  output out1,
  output out2,
  output out3,
  output out4
);

  wire and_1_out, and_2_out, and_3_out, and_4_out, and_5_out, and_6_out, and_7_out, and_8_out, and_9_out,
       and_10_out, and_11_out, and_12_out, and_13_out, and_14_out, and_15_out, and_16_out, and_17_out,
       and_18_out, and_19_out, and_20_out, and_21_out, and_22_out, not_1_out, not_2_out, not_3_out,
       not_4_out, not_5_out, not_6_out, not_7_out, not_8_out, not_9_out, not_10_out, not_11_out, not_12_out;

  not not_1 (not_1_out, ADD);
  not not_2 (not_2_out, SUB);
  not not_3 (not_3_out, MUL);
  not not_4 (not_4_out, DIV);
  not not_5 (not_5_out, LSR);
  not not_6 (not_6_out, LSL);
  not not_7 (not_7_out, RSR);
  not not_8 (not_8_out, RSL);
  not not_9 (not_9_out, MOV);
  not not_10 (not_10_out, MOD);
  not not_11 (not_11_out, CMP);
  not not_12 (not_12_out, TST);
  and and_1 (and_1_out, not_1_out, not_11_out, not_4_out, not_6_out, not_5_out, not_10_out, not_9_out, not_3_out, not_8_out, not_7_out, not_2_out, TST);
  and and_2 (and_2_out, not_1_out, CMP, not_4_out, not_6_out, not_5_out, not_10_out, not_9_out, not_3_out, not_8_out, not_7_out, not_2_out, not_12_out);
  and and_3 (and_3_out, not_1_out, not_11_out, not_4_out, not_6_out, not_5_out, MOD, not_9_out, not_3_out, not_8_out, not_7_out, not_2_out, not_12_out);
  and and_4 (and_4_out, not_1_out, not_11_out, not_4_out, not_6_out, not_5_out, not_10_out, MOV, not_3_out, not_8_out, not_7_out, not_2_out, not_12_out);
  and and_5 (and_5_out, not_1_out, not_11_out, not_4_out, not_6_out, not_5_out, not_10_out, not_9_out, not_3_out, RSL, not_7_out, not_2_out, not_12_out);
  and and_6 (and_6_out, not_1_out, not_11_out, not_4_out, not_6_out, not_5_out, not_10_out, not_9_out, not_3_out, not_8_out, not_7_out, not_2_out, TST);
  and and_7 (and_7_out, not_1_out, not_11_out, not_4_out, not_6_out, not_5_out, not_10_out, not_9_out, not_3_out, not_8_out, RSR, not_2_out, not_12_out);
  and and_8 (and_8_out, not_1_out, not_11_out, not_4_out, LSL, not_5_out, not_10_out, not_9_out, not_3_out, not_8_out, not_7_out, not_2_out, not_12_out);
  and and_9 (and_9_out, not_1_out, not_11_out, not_4_out, not_6_out, LSR, not_10_out, not_9_out, not_3_out, not_8_out, not_7_out, not_2_out, not_12_out);
  and and_10 (and_10_out, not_1_out, not_11_out, DIV, not_6_out, not_5_out, not_10_out, not_9_out, not_3_out, not_8_out, not_7_out, not_2_out, not_12_out);
  and and_11 (and_11_out, not_1_out, CMP, not_4_out, not_6_out, not_5_out, not_10_out, not_9_out, not_3_out, not_8_out, not_7_out, not_2_out, not_12_out);
  and and_12 (and_12_out, not_1_out, not_11_out, not_4_out, not_6_out, not_5_out, MOD, not_9_out, not_3_out, not_8_out, not_7_out, not_2_out, not_12_out);
  and and_13 (and_13_out, not_1_out, not_11_out, not_4_out, not_6_out, not_5_out, not_10_out, not_9_out, not_3_out, not_8_out, RSR, not_2_out, not_12_out);
  and and_14 (and_14_out, not_1_out, not_11_out, not_4_out, LSL, not_5_out, not_10_out, not_9_out, not_3_out, not_8_out, not_7_out, not_2_out, not_12_out);
  and and_15 (and_15_out, not_1_out, not_11_out, not_4_out, not_6_out, not_5_out, not_10_out, not_9_out, MUL, not_8_out, not_7_out, not_2_out, not_12_out);
  and and_16 (and_16_out, not_1_out, not_11_out, not_4_out, not_6_out, not_5_out, not_10_out, not_9_out, not_3_out, not_8_out, not_7_out, SUB, not_12_out);
  and and_17 (and_17_out, not_1_out, CMP, not_4_out, not_6_out, not_5_out, not_10_out, not_9_out, not_3_out, not_8_out, not_7_out, not_2_out, not_12_out);
  and and_18 (and_18_out, not_1_out, not_11_out, not_4_out, not_6_out, not_5_out, not_10_out, MOV, not_3_out, not_8_out, not_7_out, not_2_out, not_12_out);
  and and_19 (and_19_out, not_1_out, not_11_out, not_4_out, not_6_out, not_5_out, not_10_out, not_9_out, not_3_out, not_8_out, RSR, not_2_out, not_12_out);
  and and_20 (and_20_out, not_1_out, not_11_out, not_4_out, not_6_out, LSR, not_10_out, not_9_out, not_3_out, not_8_out, not_7_out, not_2_out, not_12_out);
  and and_21 (and_21_out, not_1_out, not_11_out, not_4_out, not_6_out, not_5_out, not_10_out, not_9_out, MUL, not_8_out, not_7_out, not_2_out, not_12_out);
  and and_22 (and_22_out, ADD, not_11_out, not_4_out, not_6_out, not_5_out, not_10_out, not_9_out, not_3_out, not_8_out, not_7_out, not_2_out, not_12_out);
  or or_1 (out1, and_1_out, and_2_out, and_3_out, and_4_out, and_5_out);
  or or_2 (out2, and_6_out, and_7_out, and_8_out, and_9_out, and_10_out);
  or or_3 (out3, and_11_out, and_12_out, and_13_out, and_14_out, and_15_out, and_16_out);
  or or_4 (out4, and_17_out, and_18_out, and_19_out, and_20_out, and_21_out, and_22_out);
endmodule
