// Digital circuit conv_OH_to_Num_LogicalOPs.dig as structural Verilog
module conv_OH_to_Num_LogicalOPs (
  input  AND,
  input  OR,
  input  XOR,
  input  NOT,
  output out1,
  output out2,
  output out3
);

  wire and_2_out, and_3_out, and_4_out, and_5_out, not_1_out, not_2_out, not_3_out, not_4_out;

  not not_1 (not_1_out, AND);
  not not_2 (not_2_out, OR);
  not not_3 (not_3_out, XOR);
  not not_4 (not_4_out, NOT);
  and and_1 (out1, not_1_out, NOT, not_2_out, not_3_out);
  and and_2 (and_2_out, not_1_out, not_4_out, not_2_out, XOR);
  and and_3 (and_3_out, not_1_out, not_4_out, OR, not_3_out);
  and and_4 (and_4_out, not_1_out, not_4_out, not_2_out, XOR);
  and and_5 (and_5_out, AND, not_4_out, not_2_out, not_3_out);
  or or_1 (out2, and_2_out, and_3_out);
  or or_2 (out3, and_4_out, and_5_out);
endmodule
