// Digital circuit fic.dig as structural Verilog
module fic (
  input  clk,
  input  in_2,
  input  in_3,
  input  in_4,
  input  in_5
);

  wire instructionregister_1_p4, IR_en, jmp_sel, ld, load, main_memory_1_p2, PC_en, program_counter_1_p2,
       program_counter_1_p6, registers_1_p5, st, store_en, \type ;
  wire [1:0] store;
  wire [15:0] ACC_q, demultiplexer_1_out_0, demultiplexer_1_out_1, instructionregister_1_p5,
       main_memory_1_p5, multiplexer_1_out, mux_16b_3_la_1_1_p4, program_counter_1_p5;

  // Program_Counter program_counter_1: pin names not known; wires that end beside it: clk, program_counter_1_p2, PC_en, jmp_sel, program_counter_1_p5, program_counter_1_p6, program_counter_1_p6
  // Control_Unit_Impl control_unit_impl_1: pin names not known; wires that end beside it: demultiplexer_1_out_0[15:10]
  Multiplexer #(.Selector_Bits(2), .Bits(16)) multiplexer_1 (
    .sel(store), .in_1(program_counter_1_p5), .in_2(instructionregister_1_p5), .in_3(mux_16b_3_la_1_1_p4),
    .out(multiplexer_1_out));  // open: in_0
  // main_memory main_memory_1: pin names not known; wires that end beside it: multiplexer_1_out, main_memory_1_p2, st, ld, main_memory_1_p5
  Demultiplexer #(.Bits(16)) demultiplexer_1 (
    .sel(load), .in(main_memory_1_p5), .out_0(demultiplexer_1_out_0), .out_1(demultiplexer_1_out_1));
  assign main_memory_1_p2 = store_en ? registers_1_p5 : 1'bz;  // Driver driver_1
  // InstructionRegister instructionregister_1: pin names not known; wires that end beside it: demultiplexer_1_out_0[9:0], IR_en, \type , instructionregister_1_p4, instructionregister_1_p5, program_counter_1_p2
  Register #(.Bits(16)) ACC (.Q(ACC_q));  // open: D, C, en
  // mux_16b_3_la_1 mux_16b_3_la_1_1: pin names not known; wires that end beside it: instructionregister_1_p5, demultiplexer_1_out_1, load, mux_16b_3_la_1_1_p4
  // Registers registers_1: pin names not known; wires that end beside it: instructionregister_1_p4, instructionregister_1_p4, mux_16b_3_la_1_1_p4, load, registers_1_p5

  // Notes on the sheet:
  //   clk: Hz: 10
endmodule
