// Digital circuit main_memory.dig as structural Verilog
module main_memory (
  input  [9:0] adr_in,
  input  clk,
  input  [15:0] D_in,
  input  str,
  input  ld,
  output [15:0] D_out
);

  RAMDualPort #(.AddrBits(10), .isProgramMemory("true"), .Bits(16)) RAM_separatedPorts (
    .A(adr_in), .Din(D_in), .str(str), .C(clk), .ld(ld), .D(D_out));

  // Notes on the sheet:
  //   adr_in: Adresa la care se scriu/citesc datele
  //   str: control signal
  //   ld: control signal
endmodule
