// Digital circuit mux_16b_3_la_1.dig as structural Verilog
module mux_16b_3_la_1 (
  input  [8:0] immediate,
  input  [15:0] memData,
  input  sel,
  output [15:0] D_out
);

  Multiplexer #(.Bits(16)) multiplexer_1 (.sel(sel), .in_0(memData), .in_1({{7{1'b0}}, immediate}), .out(D_out));
endmodule
