// Digital circuit opcode_is_branch.dig as structural Verilog
module opcode_is_branch (
  input  A,
  input  B,
  input  C,
  input  D,
  input  E,
  input  F,
  output Y
);

  wire and_1_out, and_2_out, and_3_out, not_1_out, not_2_out, not_3_out, not_4_out, not_5_out, not_6_out;

  not not_1 (not_1_out, A);
  not not_2 (not_2_out, B);
  not not_3 (not_3_out, C);
  not not_4 (not_4_out, D);
  not not_5 (not_5_out, E);
  not not_6 (not_6_out, F);
  and and_1 (and_1_out, not_1_out, not_2_out, C, not_4_out, not_5_out, not_6_out);
  and and_2 (and_2_out, not_1_out, not_2_out, not_3_out, E);
  and and_3 (and_3_out, not_1_out, not_2_out, not_3_out, D);
  or or_1 (Y, and_1_out, and_2_out, and_3_out);
endmodule
